// Logisim project PRO2.circ as structural Verilog: 1 circuit, main circuit main
module main (
  input  in_1,
  input  in_2,
  input  A,
  input  in_4,
  input  A_2,
  input  in_6,
  output out_7,
  output out_8,
  output out_9
);

  wire nand_2_out, nand_3_out, nand_4_out, nand_5_out;

  nand nand_1 (out_7, in_1, in_2);
  nand nand_2 (nand_2_out, A, in_4);
  nand nand_3 (nand_3_out, A_2, A_2);
  nand nand_4 (nand_4_out, in_6, in_6);
  nand nand_5 (nand_5_out, nand_2_out, nand_2_out);
  nand nand_6 (out_9, nand_3_out, nand_4_out);
  nand nand_7 (out_8, nand_5_out, nand_5_out);

  // Notes on the sheet:
  //   2
  //   NOT gate using NAND gate
  //   B
  //   y=ANANDA=A'
  //   AND gate useing NAND GATE
  //   B
  //   Y=A'
  //   Y=(A NAND B) NAND(A NAND B)
  //   Y=(A NAND A)NAND(B NANDB)=A+B
  //   Y=A+B
  //   Y=A.B
endmodule
