// Logisim project PRO8.circ as structural Verilog: 1 circuit, main circuit main
module main (
  input  A,
  input  B,
  input  in_3,
  output out_4,
  output out_5
);

  wire and_1_out, and_2_out, and_3_out, xor_1_out;

  xor xor_1 (xor_1_out, A, B);
  and and_1 (and_1_out, B, B);
  and and_2 (and_2_out, A, in_3);
  and and_3 (and_3_out, A, B);
  xor xor_2 (out_4, xor_1_out, in_3);
  or or_1 (out_5, and_1_out, and_2_out, and_3_out);

  // Notes on the sheet:
  //   8)
  //   C
  //   FULL ADDER
  //   Y=A+B+C,C+AC+AB
  //   A+B
  //   A+B+C
  //   BC+AC+AB
endmodule
