// Logisim project PROGAM1.circ as structural Verilog: 1 circuit, main circuit main
module main (
  input  A,
  input  A_2,
  input  in_3,
  input  B,
  input  B_2,
  input  A_3,
  input  in_7,
  input  in_8,
  input  B_3,
  input  in_10,
  input  in_11,
  input  in_12,
  input  in_13,
  output out_14,
  output out_15,
  output out_16,
  output out_17,
  output out_18,
  output out_19,
  output out_20
);

  and and_1 (out_14, A, B);
  nand nand_1 (out_17, A_3, B_3);
  xnor xnor_1 (out_20, in_12, in_13);
  or or_1 (out_15, A_2, B_2);
  nor nor_1 (out_18, in_7, in_10);
  not not_1 (out_16, in_3);
  xor xor_1 (out_19, in_8, in_11);

  // Notes on the sheet:
  //   1
  //   AND GATES
  //   NAND GATE
  //   XNOR GATE
  //   Y=A.B
  //   Y=A.B
  //   OR GATE
  //   NOR GATE
  //   Y=A+B
  //   A
  //   NOT GATE
  //   XOR GATE
  //   A=A'
endmodule
