// Logisim project PROGRAM3.circ as structural Verilog: 1 circuit, main circuit main
module main (
  input  in_1,
  input  A,
  input  B,
  input  in_4,
  input  in_5,
  output out_6,
  output out_7,
  output out_8
);

  wire nor_2_out, nor_3_out, nor_4_out;

  nor nor_1 (out_6, in_1, in_1);
  not nor_2 (nor_2_out, A);  // NOR_Gate
  not nor_3 (nor_3_out, B);  // NOR_Gate
  nor nor_4 (nor_4_out, in_4, in_5);
  nor nor_5 (out_7, nor_2_out, nor_3_out);
  nor nor_6 (out_8, nor_4_out, nor_4_out);

  // Notes on the sheet:
  //   3
  //   NOT GATE USEING NOR GATE
  //   AND GATE USEING NOR GATE
  //   OR GAATE useing NOR gate
  //   Y=A NOR A=A'
  //   y=(A NOR B) NOR(A NORB)=A+B
  //   Y=A.B
endmodule
