// Logisim project PROGRAM4.circ as structural Verilog: 2 circuits, main circuit main
module main (
  input  a,
  input  b,
  input  A_2,
  input  B_2,
  input  A_3,
  input  in_6,
  input  A_4,
  input  B_3,
  output out_9,
  output out_10,
  output out_11,
  output out_12
);

  wire and_1_out, not_1_out, not_2_out, not_3_out, not_4_out, or_1_out;

  not not_1 (not_1_out, A_2);
  not not_2 (not_2_out, B_2);
  not not_3 (not_3_out, A_4);
  not not_4 (not_4_out, B_3);
  or or_1 (or_1_out, a, b);
  and and_1 (and_1_out, A_3, in_6);
  not not_5 (out_9, or_1_out);
  nand nand_1 (out_10, not_1_out, not_2_out);
  not not_6 (out_11, and_1_out);
  or or_2 (out_12, not_3_out, not_4_out);

  // Notes on the sheet:
  //   4
  //   a
  //   b
  //   A
  //   B
  //   B
  //   not(a+b)=(a'+b'
  //   )
  //   (not A.).(notB. )=a'.b'.
  //   NOT(A.B)=(A'.B')
  //   y=(a'+b')
  //   Y=A'+B'
  //   Y=A'+B'
  //   Y=A'.B'
endmodule

module KMAP (
  input  A,
  input  B,
  input  C,
  output F
);

  wire and_1_out, not_1_out;

  not not_1 (not_1_out, A);
  and and_1 (and_1_out, not_1_out, B);
  or or_1 (F, C, and_1_out);
endmodule
