// Logisim project PROGRAM5.circ as structural Verilog
module kmap (
  input  a,
  input  b,
  input  c,
  input  B_2,
  input  in_5,
  input  A_2,
  output f,
  output out_8
);

  wire and_1_out, and_2_out, and_3_out, and_4_out, and_5_out, and_6_out, not_1_out, not_2_out, not_3_out,
       not_4_out;

  not not_1 (not_1_out, a);
  and and_1 (and_1_out, not_1_out, b);
  not not_2 (not_2_out, A_2);
  or or_1 (f, c, and_1_out);
  not not_3 (not_3_out, B_2);
  not not_4 (not_4_out, in_5);
  and and_2 (and_2_out, not_2_out, not_3_out, in_5);
  and and_3 (and_3_out, not_2_out, B_2, not_4_out);
  and and_4 (and_4_out, B_2, B_2, in_5);
  and and_5 (and_5_out, A_2, not_3_out, in_5);
  and and_6 (and_6_out, A_2, B_2, in_5);
  or or_2 (out_8, and_2_out, and_3_out, and_4_out, and_5_out, and_6_out);

  // Notes on the sheet:
  //   C
  //   A'BC'
  //   A'BC
  //   AB'C
  //   ABC
  //   A'B'C
endmodule
