// Logisim project PROGRAM9.circ as structural Verilog: 1 circuit, main circuit main
module main (
  input  A,
  input  in_2,
  output out_3
);

  wire and_1_out, not_1_out;

  not not_1 (not_1_out, A);
  xor xor_1 (out_3, A, in_2);
  and and_1 (and_1_out, not_1_out, in_2);

  // Notes on the sheet:
  //   9
  //   B
  //   HALF SUBSTRACTOR
  //   Y=A+B,A'B
  //   A+B
  //   A'B
endmodule
